# Fritzing sketch CPReady (saved by Fritzing 0.9.3b)
breadboards: 1

parts:
  Part1 = Arduino Uno (Rev3)
  R1 = TRIMPOT [package=3362u-2]
  U1 = LCD-16X2 [package=lcd-16x2]
  J1 = Basic Force Sensing Resistor (FSR) [package=THT]
  R2 = Resistor [tolerance=±5% resistance=10k package="1206 [SMD]"]
  SG1 = Buzzer 12mm [package=buzzer-ccv]

nets:
  N1: Part1.A0, J1.pin_0, R2.Pin_1
  N2: Part1.D8, SG1.1
  N3: Part1.D11_PWM/MOSI, U1.E
  N4: Part1.D12/MISO, U1.RS
  N5: Part1.D2, U1.DB7
  N6: Part1.D3_PWM, U1.DB6
  N7: Part1.D5_PWM, U1.DB4
  N8: Part1.D6_PWM, U1.DB5
  5V: Part1.5V, R1.CCW, U1.VDD, U1.A, J1.pin_1, SG1.2
  GND: Part1.GND, R1.CW, U1.VSS, U1.R_W, U1.K, R2.Pin_0
  N9: R1.WIPER, U1.VO
